# Fritzing sketch CocktailMix (saved by Fritzing 0.9.3b)
breadboards: 1

parts:
  Part1 = Arduino Nano (Rev3.0)
  J1 = Piezo Speaker
  U1 = Nokia 6100 Color LCD [package=nokia6100_lcd]
  Part2 = HX711 Weighing Sensor Module

nets:
  GND: Part1.GND, J1.pin1, U1.CS, Part2.GND
  N1: Part1.D2, U1.SCK
  N2: Part1.D3, U1.DIO
  N3: Part1.D9, J1.pin2
  5V: Part1.5V, U1.VDIGITAL, Part2.VCC
  N4: Part1.A5, Part2.CK/TX
  N5: Part1.A4, Part2.DO/RX

notes:
  Nextion NX3224T024_011R
  Touch Display
  HX711 Weighing Sensor
